# Fritzing sketch Fan controller (saved by Fritzing 1.0.2b)
breadboards: 1

parts:
  WeMos_D1_Mini1 = WeMos D1 Mini
  J1 = Power Jack [package=power_jack_pth_lock]
  FAN1 = Header 4 [package=jst-4-pth]
  FAN2 = Header 4 [package=jst-4-pth]
  DTH22 = Humidity and Temperature Sensor DHT11
  A1 = WMYCONGCONG buck converter
  R1 = Resistor [tolerance=±5% power=0.25W resistance=10k package=THT]
  R2 = Resistor [tolerance=±5% power=0.25W resistance=10k package=THT]
  Squix1 = OLED 0.96" 128x64 I2C SSD1306

nets:
  5V: WeMos_D1_Mini1.5V, DTH22.Vcc, A1.Pin_4, R1.Pin_0, R2.Pin_0, Squix1.VCC
  N1: WeMos_D1_Mini1.D1, Squix1.SCL
  N2: WeMos_D1_Mini1.D2, Squix1.SCA
  FAN 1 RPM Speed signal: WeMos_D1_Mini1.D3, FAN1.3, R1.Pin_1
  FAN 1 PWM Signal: WeMos_D1_Mini1.D4, FAN1.4
  N3: WeMos_D1_Mini1.D5, DTH22.Data
  FAN 2 RPM Speed signal: WeMos_D1_Mini1.D6, FAN2.3, R2.Pin_1
  FAN 2 PWM Signal: WeMos_D1_Mini1.D7, FAN2.4
  GND: WeMos_D1_Mini1.G, J1.GNDBREAK, FAN1.1, FAN2.1, DTH22.GND, A1.Pin_3, Squix1.GND
  N4: J1.PWR, FAN1.2, FAN2.2, A1.Pin_2

custom parts:
  Humidity and Temperature Sensor DHT11: Digital relative humidity & temperature sensor DHT11
  WMYCONGCONG buck converter: These amazing little DC-DC converters feature a wide input voltage of 4.5-24V and the output voltage can be set to one of six fixed voltages, or fully variable, just by bridging the relevant solder pads on the back of the PCB..
