# Fritzing sketch kas-sensors (saved by Fritzing 1.0.2b)
circuit board: 8.46667cm x 5.64444cm
breadboards: 1

parts:
  WeMos_D1_Mini1 = WeMos D1 Mini
  BME280 = Header BME280 [package=molex-1x4_lock]
  RAIN = Rain module header [package=molex-1x4_lock]
  PMS5003 = PMS5003 Header [package=molex-1x6-ra]
  OLED = SSD1306 128x32 Oled header [package=molex-1x4_lock]
  S1 = Momentary Switch [package=tactile-pth]
  RJ12-RAIN = RJ11 Jack [package=rj11-6]
  Relais = Relais Header [package=screwterminal-3.5mm-3_lock.007s]
  RJ12-I2C = RJ11 Jack [package=rj11-6]
  RAIN-INPUT = Header 2 [package=screwterminal-3.5mm-2_lock]

nets (from the pcb view):
  VCC: WeMos_D1_Mini1.5V, BME280.VCC, RAIN.VCC, PMS5003.VCC_5V, OLED.VCC, Relais.VCC, RJ12-I2C.2
  N1: WeMos_D1_Mini1.A0, RAIN.AO
  N2: WeMos_D1_Mini1.D0, RAIN.DO
  N3: WeMos_D1_Mini1.D1, BME280.SDA, OLED.SDA, RJ12-I2C.5
  N4: WeMos_D1_Mini1.D2, BME280.SCL, OLED.SCL, RJ12-I2C.4
  N5: WeMos_D1_Mini1.D5, S1.1, S1.2
  N6: WeMos_D1_Mini1.D6, Relais.IN
  GND: WeMos_D1_Mini1.G, BME280.GND, RAIN.GND, PMS5003.GND, OLED.GND, S1.3, S1.4, Relais.GND, RJ12-I2C.3
  N7: WeMos_D1_Mini1.RX, PMS5003.TX
  N8: WeMos_D1_Mini1.TX, PMS5003.RX
  N9: RJ12-RAIN.2, RAIN-INPUT.1
  N10: RJ12-RAIN.4, RAIN-INPUT.2

custom parts:
  Header BME280: Header 4 Standard 4-pin 0.1 header. Use with straight break away headers (SKU : PRT-00116), right angle break away headers (PRT-00553), swiss pins (PRT-00743), machine pins (PRT-00117), and female headers (PRT-00115). Molex polarized connector foot print use with SKU : PRT-08231 with associated crimp pins and housings. 1MM SMD Version SKU: PRT-10208
  Rain module header: Header 4 Standard 4-pin 0.1 header. Use with straight break away headers (SKU : PRT-00116), right angle break away headers (PRT-00553), swiss pins (PRT-00743), machine pins (PRT-00117), and female headers (PRT-00115). Molex polarized connector foot print use with SKU : PRT-08231 with associated crimp pins and housings. 1MM SMD Version SKU: PRT-10208
  PMS5003 Header: Header 6 Standard 6-pin 0.1 header. Use with straight break away headers (SKU : PRT-00116), right angle break away headers (PRT-00553), swiss pins (PRT-00743), machine pins (PRT-00117), and female headers (PRT-00115). Molex polarized connector foot print use with SKU : PRT-08094 with associated crimp pins and housings. NOTES ON THE VARIANTS LOCK and LOCK_LONGPADS... This footprint was designed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
  SSD1306 128x32 Oled header: Header 4 Standard 4-pin 0.1 header. Use with straight break away headers (SKU : PRT-00116), right angle break away headers (PRT-00553), swiss pins (PRT-00743), machine pins (PRT-00117), and female headers (PRT-00115). Molex polarized connector foot print use with SKU : PRT-08231 with associated crimp pins and housings. 1MM SMD Version SKU: PRT-10208
  Relais Header: Header 3 Standard 3-pin 0.1 header. Use with straight break away headers (SKU : PRT-00116), right angle break away headers (PRT-00553), swiss pins (PRT-00743), machine pins (PRT-00117), and female headers (PRT-00115). Molex polarized connector foot print use with SKU : PRT-08232 with associated crimp pins and housings.
